// Logisim project ReMiMo.circ as structural Verilog: 13 circuits, main circuit ReMiMo
// address
module ReMiMo (
  input  Cycle,
  input  Instr,
  input  Stop,
  input  [15:0] Addr
);

  wire alu_im, and_1_out, and_2_out, and_3_out, and_4_out, and_5_out, and_6_out, c, Clear_out, ClearScr_out,
       CLK, CLKIN, Cont_out, datawrite, dwrite, FB_LED, ir_cdh, ir_k, ir_sn, irload, n, not_1_out, pcload,
       pcrel, pcsel, Phase, RAMSel, reset, shift_en, shiftenable, TTYSel, v, z;
  wire [1:0] addrsel, aluop, dregs, regsrc, sregs;
  wire [3:0] icycles, instructionreg_1_cond, mv_shift, opcode, showhexa_1_digit, showhexa_1_out_2,
       showhexa_1_out_3, showhexa_1_out_5, showhexa_2_digit, showhexa_2_out_2, showhexa_2_out_3,
       showhexa_2_out_5;
  wire [15:0] adder_1_out, address, aluout, cmds, cycles, data, dreg, frame_buffer_16x16_1_out_6,
       frame_buffer_16x16_1_out_7, frame_buffer_16x16_1_out_8, frame_buffer_16x16_1_out_9,
       frame_buffer_16x16_1_out_10, frame_buffer_16x16_1_out_11, frame_buffer_16x16_1_out_12,
       frame_buffer_16x16_1_out_13, frame_buffer_16x16_1_out_14, frame_buffer_16x16_1_out_15,
       frame_buffer_16x16_1_out_16, frame_buffer_16x16_1_out_17, frame_buffer_16x16_1_out_18,
       frame_buffer_16x16_1_out_19, frame_buffer_16x16_1_out_20, frame_buffer_16x16_1_out_21, immed, irreg,
       movmagic_1_w_out, multiplexer_1_out, multiplexer_2_out, multiplexer_3_out, pcreg, registerfile_1_r0,
       registerfile_1_r1, registerfile_1_r2, registerfile_1_r3, sreg;

  PC pc_1 (.imreg(immed), .pcs(pcsel), .pcload(pcload), .clock(CLK), .reset(reset), .pcr(pcrel), .pcout(pcreg));
  movMagic movmagic_1 (
    .w_in(multiplexer_1_out), .shift(mv_shift), .a(ir_k), .dir(ir_cdh), .negate(ir_sn), .enable(shift_en),
    .w_out(movmagic_1_w_out));
  Multiplexer #(.select(2), .width(16)) multiplexer_1 (
    .in0(sreg), .in1(immed), .in2(data), .in3(multiplexer_2_out), .out(multiplexer_1_out), .sel(regsrc));
  Multiplexer #(.width(16)) multiplexer_2 (.in0(aluout), .in1(data), .out(multiplexer_2_out), .sel(and_1_out));
  and and_1 (and_1_out, ~alu_im, ir_k);  // AND_Gate
  Adder #(.width(16)) adder_1 (.a(immed), .b(sreg), .out(adder_1_out));  // open: cin, cout
  Multiplexer #(.width(16)) multiplexer_3 (.in0(sreg), .in1(immed), .out(multiplexer_3_out), .sel(alu_im));
  InstructionReg instructionreg_1 (
    .reset(reset), .irload(irload), .instruction(data), .clock(CLK), .f1(ir_sn),
    .Instruction_register_Content(irreg), .f3(ir_k), .shift(mv_shift), .enable_magic(shiftenable),
    .immed(immed), .opcode(opcode), .Cond(instructionreg_1_cond), .sregsel(sregs), .dregsel(dregs),
    .alu_useimmed(alu_im), .f2(ir_cdh));
  // Probe on irreg
  Button u_Reset (.out(reset));
  Multiplexer #(.enable("true"), .select(2), .width(16)) multiplexer_4 (
    .in0(pcreg), .in1(immed), .in2(adder_1_out), .in3(dreg), .out(address), .sel(addrsel));  // open: en
  // Probe on addrsel
  // Probe on registerfile_1_r0
  // Probe on registerfile_1_r1
  // Probe on registerfile_1_r2
  // Probe on registerfile_1_r3
  Registerfile registerfile_1 (
    .regval(movmagic_1_w_out), .clock(CLK), .Reset(reset), .dsel(dregs), .ssel(sregs), .dwrite(dwrite),
    .dreg(dreg), .sreg(sreg), .r0(registerfile_1_r0), .r1(registerfile_1_r1), .r2(registerfile_1_r2),
    .r3(registerfile_1_r3));
  and and_2 (and_2_out, ir_sn, Phase);
  Address_Decoder ADDR_DEC (.Address(address), .RAM(RAMSel), .FB_LED(FB_LED), .TTY(TTYSel));  // open: output_3
  ALU alu_1 (
    .wCarry(ir_cdh), .reset(reset), .A(dreg), .B(multiplexer_3_out), .aluop(aluop), .setflag(and_2_out),
    .clock(CLK), .Result(aluout), .oVerflow(v), .Zero(z), .Negative(n), .Carry(c));
  Clock SysClk (.out(CLKIN));
  assign data = datawrite ? dreg : 16'bz;  // Controlled_Buffer controlled_buffer_1
  // Probe on Phase
  LED led_1 (.in(Phase));
  LED led_2 (.in(Phase));
  // Probe on pcreg
  Hex_Digit_Display hex_digit_display_1 (.value(showhexa_1_out_2));  // open: dp
  Hex_Digit_Display hex_digit_display_2 (.value(showhexa_1_out_3));  // open: dp
  ShowHexa showhexa_1 (
    .Data(address), .Digit(showhexa_1_digit), .out_5(showhexa_1_out_5), .out_2(showhexa_1_out_2),
    .out_3(showhexa_1_out_3));
  LED led_3 (.in(datawrite));
  Hex_Digit_Display hex_digit_display_3 (.value(showhexa_2_out_2));  // open: dp
  Hex_Digit_Display hex_digit_display_4 (.value(showhexa_2_out_3));  // open: dp
  ShowHexa showhexa_2 (
    .Data(data), .Digit(showhexa_2_digit), .out_5(showhexa_2_out_5), .out_2(showhexa_2_out_2),
    .out_3(showhexa_2_out_3));
  LED led_4 (.in(datawrite));
  ControlUnit_HW controlunit_hw_1 (
    .opcode(opcode), .clock(CLK), .reset(reset), .Condition(instructionreg_1_cond), .carry(c), .negative(n),
    .oVerflow(v), .zero(z), .aluop(aluop), .readwrite(datawrite), .phase(Phase), .addrsel(addrsel),
    .dwrite(dwrite), .regsel(regsrc), .pcsel(pcsel), .irload(irload), .pcr(pcrel), .pcload(pcload),
    .shiften(shift_en));
  // Probe on address
  Hex_Digit_Display hex_digit_display_5 (.value(showhexa_1_digit));  // open: dp
  Hex_Digit_Display hex_digit_display_6 (.value(showhexa_1_out_5));  // open: dp
  LED led_5 (.in(datawrite));
  Hex_Digit_Display hex_digit_display_7 (.value(showhexa_2_digit));  // open: dp
  Hex_Digit_Display hex_digit_display_8 (.value(showhexa_2_out_5));  // open: dp
  // Probe on datawrite
  LED led_6 (.in(datawrite));
  // Probe on data
  // Probe on opcode
  // Probe on RAMSel
  // Probe on datawrite
  // Probe on TTYSel
  // Probe on FB_LED
  LED u_C (.in(c));
  LED u_Z (.in(z));
  LED u_N (.in(n));
  LED u_V (.in(v));
  // Probe on dregs
  // Probe on pcreg
  // Probe on cmds
  // Probe on dregs
  // Probe on sregs
  // Probe on sregs
  // Probe on immed
  // Probe on irreg
  // Probe on immed
  and and_3 (and_3_out, RAMSel, datawrite);
  and and_4 (and_4_out, RAMSel, not_1_out);
  not not_1 (not_1_out, datawrite);
  // Probe on cycles
  RAM #(.addrWidth(14), .asyncread("true"), .dataWidth(16), .databus("bidir"), .\type ("nonvolatile")) ram_1 (
    .addr(address[13:0]), .we(and_3_out), .oe(and_4_out), .clk(CLK), .data(data));
  Frame_Buffer_16x16 frame_buffer_16x16_1 (
    .address(address[3:0]), .store(and_5_out), .data(data), .clock(CLK), .reset(Clear_out),
    .out_6(frame_buffer_16x16_1_out_6), .out_7(frame_buffer_16x16_1_out_7),
    .out_8(frame_buffer_16x16_1_out_8), .out_9(frame_buffer_16x16_1_out_9),
    .out_10(frame_buffer_16x16_1_out_10), .out_11(frame_buffer_16x16_1_out_11),
    .out_12(frame_buffer_16x16_1_out_12), .out_13(frame_buffer_16x16_1_out_13),
    .out_14(frame_buffer_16x16_1_out_14), .out_15(frame_buffer_16x16_1_out_15),
    .out_16(frame_buffer_16x16_1_out_16), .out_17(frame_buffer_16x16_1_out_17),
    .out_18(frame_buffer_16x16_1_out_18), .out_19(frame_buffer_16x16_1_out_19),
    .out_20(frame_buffer_16x16_1_out_20), .out_21(frame_buffer_16x16_1_out_21));
  and and_5 (and_5_out, FB_LED, datawrite);
  Button Cont (.out(Cont_out));
  // Probe on data[6:0]
  TTY #(.cols(16), .rows(4)) tty_1 (.data(data[6:0]), .clk(CLK), .we(and_6_out), .clr(ClearScr_out));
  and and_6 (and_6_out, TTYSel, datawrite);
  DotMatrix #(.inputtype("row"), .matrixcols(16), .matrixrows(16)) dotmatrix_1 (
    .row0(frame_buffer_16x16_1_out_21), .row1(frame_buffer_16x16_1_out_20),
    .row2(frame_buffer_16x16_1_out_19), .row3(frame_buffer_16x16_1_out_18),
    .row4(frame_buffer_16x16_1_out_17), .row5(frame_buffer_16x16_1_out_16),
    .row6(frame_buffer_16x16_1_out_15), .row7(frame_buffer_16x16_1_out_14),
    .row8(frame_buffer_16x16_1_out_13), .row9(frame_buffer_16x16_1_out_12),
    .row10(frame_buffer_16x16_1_out_11), .row11(frame_buffer_16x16_1_out_10),
    .row12(frame_buffer_16x16_1_out_9), .row13(frame_buffer_16x16_1_out_8),
    .row14(frame_buffer_16x16_1_out_7), .row15(frame_buffer_16x16_1_out_6));
  Button ClearScr (.out(ClearScr_out));
  Button Clear (.out(Clear_out));
  DebugUnit debugunit_1 (
    .reset(reset), .\continue (Cont_out), .clock(CLKIN), .pcreg(pcreg), .break_addr(Addr),
    .break_on_addr(Stop), .ucounter(Phase), .break_on_instr(Instr), .break_on_cycle(Cycle), .clock_out(CLK));
  Counters counters_1 (
    .new_ucounter(Phase), .reset(reset), .clock(CLK), .cmds(cmds), .cycles(cycles), .icycles(icycles));

  // Other names for the same wires on the sheet: dbgadr = Stop

  // Notes on the sheet:
  //   ReMiMo 
  //   Quick tips:
  //   v05: Migration to EVO, Debug, Counters, ImmReg Units
  //   Based on: https://minnie.tuhs.org/CompArch/Tutes/week03.html
  //   1.0
  //   Registers
  //   Use ctrl+t to manually toggle global clock signal
  //   Use Simulate->Ticks Enabled for automatic clock signal
  //   ReMiMo(Matic Babnik): redo instruction set
  //   v06: More V.N. model like design (CPU,Mem,IO,..)
  //   Fetch
  //   Execute
  //   Read
  //   Data BUS
  //   Read
  //   Address
  //   Address BUS
  //   Control BUS
  //   Write
  //   Write
  //   Data
  //   Flags
  //   Instruction:
  //   Rd
  //   Rs
  //   immed 
  //   RAM
  //   TTY
  //   Debug
  //   Breakpoint
  //   Frame Buffer LED 16x16
endmodule

module InstructionReg (
  input  [15:0] instruction,
  input  reset,
  input  clock,
  input  irload,
  output [1:0] sregsel,
  output [1:0] dregsel,
  output [3:0] opcode,
  output [15:0] immed,
  output [3:0] Cond,
  output [15:0] Instruction_register_Content,
  output alu_useimmed,
  output f1,
  output f3,
  output f2,
  output [3:0] shift,
  output enable_magic
);

  wire and_4_out, and_5_out, is_mov_immd;
  wire [1:0] xor_1_out;
  wire [3:0] multiplexer_2_out;
  wire [15:0] immd_a, immd_i8, immd_u8, immd_u12;

  assign xor_1_out = Cond[1:0] ^ Cond[3:2];  // XOR_Gate xor_1, 2 bits wide
  and and_1 (alu_useimmed, ~xor_1_out[0], ~xor_1_out[1]);  // AND_Gate
  Multiplexer #(.select(4)) multiplexer_1 (
    .in0(Instruction_register_Content[7]), .in1(Instruction_register_Content[7]),
    .in2(Instruction_register_Content[7]), .in3(Instruction_register_Content[7]), .in4(1'b0), .in5(1'b0),
    .in6(Instruction_register_Content[7]), .in7(Cond[1]), .in8(1'b0), .in9(1'b0), .in10(1'b0), .in11(1'b0),
    .in12(1'b0), .in13(1'b0), .in14(1'b0), .in15(1'b0), .out(f1), .sel(Instruction_register_Content[15:12]));
  and and_2 (is_mov_immd, Instruction_register_Content[12], enable_magic);
  and and_3 (enable_magic, Instruction_register_Content[13], Instruction_register_Content[14], ~Instruction_register_Content[15]);  // AND_Gate
  Register #(.width(16)) register_1 (
    .D(instruction), .en(irload),
    .Q({Instruction_register_Content[15:12], Cond, Instruction_register_Content[7:0]}), .clk(clock),
    .clr(reset));
  Multiplexer #(.width(4)) multiplexer_2 (.in0(4'b0000), .in1(4'b1000), .out(multiplexer_2_out), .sel(Cond[0]));
  assign immd_a = {{9{1'b0}}, Instruction_register_Content[6:0]};  // Bit_Extender bit_extender_1
  assign immd_u8 = {{8{1'b0}}, Instruction_register_Content[7:0]};  // Bit_Extender bit_extender_2
  assign immd_i8 = {{8{Instruction_register_Content[7]}}, Instruction_register_Content[7:0]};  // Bit_Extender bit_extender_3
  assign immd_u12 = {{4{1'b0}}, {Cond, Instruction_register_Content[7:0]}};  // Bit_Extender bit_extender_4
  and and_4 (and_4_out, ~alu_useimmed, Instruction_register_Content[5]);  // AND_Gate
  Multiplexer #(.select(4)) multiplexer_3 (
    .in0(and_4_out), .in1(and_4_out), .in2(and_4_out), .in3(and_4_out), .in4(1'b0), .in5(1'b0),
    .in6(Instruction_register_Content[5]), .in7(1'b0), .in8(1'b0), .in9(1'b0), .in10(1'b0), .in11(1'b0),
    .in12(1'b0), .in13(1'b0), .in14(1'b0), .in15(1'b0), .out(f3), .sel(Instruction_register_Content[15:12]));
  Multiplexer #(.width(4)) multiplexer_4 (
    .in0(Instruction_register_Content[3:0]), .in1(multiplexer_2_out), .out(shift), .sel(is_mov_immd));
  Multiplexer #(.select(4), .width(16)) multiplexer_5 (
    .in0(immd_a), .in1(immd_a), .in2(immd_a), .in3(immd_a), .in4(immd_u8), .in5(immd_u8), .in6({16{1'b0}}),
    .in7(immd_u8), .in8(immd_u12), .in9(immd_i8), .in10({16{1'b0}}), .in11({16{1'b0}}), .in12({16{1'b0}}),
    .in13({16{1'b0}}), .in14({16{1'b0}}), .in15({16{1'b0}}), .out(immed),
    .sel(Instruction_register_Content[15:12]));
  and and_5 (and_5_out, ~alu_useimmed, Instruction_register_Content[6]);  // AND_Gate
  Multiplexer #(.select(4)) multiplexer_6 (
    .in0(and_5_out), .in1(and_5_out), .in2(and_5_out), .in3(and_5_out), .in4(1'b0), .in5(1'b0),
    .in6(Instruction_register_Content[6]), .in7(1'b0), .in8(1'b0), .in9(1'b0), .in10(1'b0), .in11(1'b0),
    .in12(1'b0), .in13(1'b0), .in14(1'b0), .in15(1'b0), .out(f2), .sel(Instruction_register_Content[15:12]));

  assign dregsel = Cond[3:2];
  assign Instruction_register_Content[11:8] = Cond;
  assign opcode = Instruction_register_Content[15:12];
  assign sregsel = Cond[1:0];

  // Other names for the same wires on the sheet: alu_immd = alu_useimmed;
  //   instruction_t[15:0] = {Instruction_register_Content[15:12], Cond, Instruction_register_Content[7:0]};
  //   rs[1:0] = Cond[1:0]; rd[1:0] = Cond[3:2]; is_mov = enable_magic

  // Notes on the sheet:
  //   IR Logic
  //   S,N
  //   F
  //   C,D
endmodule

module Registerfile (
  input  [15:0] regval,
  input  Reset,
  input  [1:0] dsel,
  input  [1:0] ssel,
  input  dwrite,
  input  clock,
  output [15:0] r0,
  output [15:0] r1,
  output [15:0] r2,
  output [15:0] r3,
  output [15:0] dreg,
  output [15:0] sreg
);

  wire demultiplexer_1_out0, demultiplexer_1_out1, demultiplexer_1_out2, demultiplexer_1_out3;

  Demultiplexer #(.select(2)) demultiplexer_1 (
    .out0(demultiplexer_1_out0), .out1(demultiplexer_1_out1), .out2(demultiplexer_1_out2),
    .out3(demultiplexer_1_out3), .in(dwrite), .sel(dsel));
  // Probe on regval
  // Probe on regval
  // Probe on dsel
  // Probe on ssel
  Register #(.width(16)) register_1 (.D(regval), .en(demultiplexer_1_out0), .Q(r0), .clk(clock), .clr(Reset));
  Register #(.width(16)) register_2 (.D(regval), .en(demultiplexer_1_out1), .Q(r1), .clk(clock), .clr(Reset));
  Register #(.width(16)) register_3 (.D(regval), .en(demultiplexer_1_out2), .Q(r2), .clk(clock), .clr(Reset));
  Register #(.width(16)) register_4 (.D(regval), .en(demultiplexer_1_out3), .Q(r3), .clk(clock), .clr(Reset));
  Multiplexer #(.select(2), .width(16)) multiplexer_1 (.in0(r0), .in1(r1), .in2(r2), .in3(r3), .out(dreg), .sel(dsel));
  // Probe on dreg
  Multiplexer #(.select(2), .width(16)) multiplexer_2 (.in0(r0), .in1(r1), .in2(r2), .in3(r3), .out(sreg), .sel(ssel));
  // Probe on sreg
  // Probe on r0
  // Probe on r0
  // Probe on r1
  // Probe on r1
  // Probe on r2
  // Probe on r2
  // Probe on r3
  // Probe on r3

  // Notes on the sheet:
  //   Rd select
  //   Rs select
  //   Register File
  //   Rd
  //   R0
  //   R1
  //   R2
  //   R3
  //   Rs
endmodule

module ALU (
  input  wCarry,
  input  [15:0] A,
  input  [15:0] B,
  input  [1:0] aluop,
  input  setflag,
  input  clock,
  input  reset,
  output Carry,
  output Zero,
  output Negative,
  output [15:0] Result,
  output oVerflow
);

  wire adder_1_cout, and_1_out, and_3_out, and_4_out, multiplexer_2_out, multiplexer_3_out, nor_1_out,
       subtractor_1_bout, xnor_1_out, xnor_2_out, xor_1_out, xor_2_out;
  wire [15:0] adder_1_out, and_2_out, or_1_out, subtractor_1_out;

  and and_1 (and_1_out, Carry, wCarry);
  xnor xnor_1 (xnor_1_out, A[15], B[15]);
  xor xor_1 (xor_1_out, B[15], Result[15]);
  xnor xnor_2 (xnor_2_out, Result[15], B[15]);
  xor xor_2 (xor_2_out, B[15], A[15]);
  Subtractor #(.width(16)) subtractor_1 (
    .a(A), .b(B), .out(subtractor_1_out), .bin(and_1_out), .bout(subtractor_1_bout));
  Adder #(.width(16)) adder_1 (.a(A), .b(B), .out(adder_1_out), .cin(and_1_out), .cout(adder_1_cout));
  assign or_1_out = A | B;  // OR_Gate or_1, 16 bits wide
  assign and_2_out = A & B;  // AND_Gate and_2, 16 bits wide
  and and_3 (and_3_out, xnor_1_out, xor_1_out);
  and and_4 (and_4_out, xnor_2_out, xor_2_out);
  Multiplexer #(.select(2), .width(16)) multiplexer_1 (
    .in0(and_2_out), .in1(or_1_out), .in2(adder_1_out), .in3(subtractor_1_out), .out(Result), .sel(aluop));
  Multiplexer #(.select(2)) multiplexer_2 (
    .in0(1'b0), .in1(1'b0), .in2(adder_1_cout), .in3(subtractor_1_bout), .out(multiplexer_2_out), .sel(aluop));
  Multiplexer #(.select(2)) multiplexer_3 (
    .in0(1'b0), .in1(1'b0), .in2(and_3_out), .in3(and_4_out), .out(multiplexer_3_out), .sel(aluop));
  nor nor_1 (nor_1_out, Result[0], Result[1], Result[2], Result[3], Result[4], Result[5], Result[6], Result[7], Result[9], Result[10], Result[11], Result[12], Result[13], Result[14], Result[15], Result[8]);
  Register #(.width(1)) register_1 (.D(multiplexer_2_out), .en(setflag), .clk(clock), .Q(Carry), .clr(reset));
  Register #(.width(1)) register_2 (.D(nor_1_out), .en(setflag), .clk(clock), .Q(Zero), .clr(reset));
  Register #(.width(1)) register_3 (.D(Result[15]), .en(setflag), .clk(clock), .Q(Negative), .clr(reset));
  Register #(.width(1)) register_4 (.D(multiplexer_3_out), .en(setflag), .clk(clock), .Q(oVerflow), .clr(reset));

  // Other names for the same wires on the sheet: signA = A[15]; signB = B[15]; PrevCarry = Carry; signR = Result[15]
endmodule

module PC (
  input  [15:0] imreg,
  input  pcs,
  input  pcload,
  input  clock,
  input  reset,
  input  pcr,
  output [15:0] pcout
);

  wire [15:0] adder_1_out, multiplexer_1_out, multiplexer_2_out;

  Multiplexer #(.width(16)) multiplexer_1 (.in0(16'h1), .in1(imreg), .out(multiplexer_1_out), .sel(pcr));
  Adder #(.width(16)) adder_1 (.a(pcout), .b(multiplexer_1_out), .out(adder_1_out));  // open: cin, cout
  Multiplexer #(.width(16)) multiplexer_2 (.in0(imreg), .in1(adder_1_out), .out(multiplexer_2_out), .sel(pcs));
  Register #(.width(16)) register_1 (.D(multiplexer_2_out), .en(pcload), .Q(pcout), .clk(clock), .clr(reset));

  // Other names for the same wires on the sheet: curPC[15:0] = pcout; x[15:0] = imreg

  // Notes on the sheet:
  //   PC Logic
endmodule

module ShowHexa (
  input  [15:0] Data,
  output [3:0] out_2,
  output [3:0] out_3,
  output [3:0] Digit,
  output [3:0] out_5
);


  assign Digit = Data[7:4];
  assign out_2 = Data[15:12];
  assign out_3 = Data[11:8];
  assign out_5 = Data[3:0];
endmodule

module Frame_Buffer_16x16 (
  input  [3:0] address,
  input  store,
  input  [15:0] data,
  input  clock,
  input  reset,
  output [15:0] out_6,
  output [15:0] out_7,
  output [15:0] out_8,
  output [15:0] out_9,
  output [15:0] out_10,
  output [15:0] out_11,
  output [15:0] out_12,
  output [15:0] out_13,
  output [15:0] out_14,
  output [15:0] out_15,
  output [15:0] out_16,
  output [15:0] out_17,
  output [15:0] out_18,
  output [15:0] out_19,
  output [15:0] out_20,
  output [15:0] out_21
);

  wire demultiplexer_1_out0, demultiplexer_1_out1, demultiplexer_1_out2, demultiplexer_1_out3,
       demultiplexer_1_out4, demultiplexer_1_out5, demultiplexer_1_out6, demultiplexer_1_out7,
       demultiplexer_1_out8, demultiplexer_1_out9, demultiplexer_1_out10, demultiplexer_1_out11,
       demultiplexer_1_out12, demultiplexer_1_out13, demultiplexer_1_out14, demultiplexer_1_out15;

  Demultiplexer #(.select(4)) demultiplexer_1 (
    .out0(demultiplexer_1_out0), .out1(demultiplexer_1_out1), .out2(demultiplexer_1_out2),
    .out3(demultiplexer_1_out3), .out4(demultiplexer_1_out4), .out5(demultiplexer_1_out5),
    .out6(demultiplexer_1_out6), .out7(demultiplexer_1_out7), .out8(demultiplexer_1_out8),
    .out9(demultiplexer_1_out9), .out10(demultiplexer_1_out10), .out11(demultiplexer_1_out11),
    .out12(demultiplexer_1_out12), .out13(demultiplexer_1_out13), .out14(demultiplexer_1_out14),
    .out15(demultiplexer_1_out15), .in(store), .sel(address));
  Register #(.width(16)) register_1 (.D(data), .en(demultiplexer_1_out0), .Q(out_6), .clk(clock), .clr(reset));
  Register #(.width(16)) register_2 (.D(data), .en(demultiplexer_1_out1), .Q(out_7), .clk(clock), .clr(reset));
  Register #(.width(16)) register_3 (.D(data), .en(demultiplexer_1_out2), .Q(out_8), .clk(clock), .clr(reset));
  Register #(.width(16)) register_4 (.D(data), .en(demultiplexer_1_out3), .Q(out_9), .clk(clock), .clr(reset));
  Register #(.width(16)) register_5 (.D(data), .en(demultiplexer_1_out4), .Q(out_10), .clk(clock), .clr(reset));
  Register #(.width(16)) register_6 (.D(data), .en(demultiplexer_1_out5), .Q(out_11), .clk(clock), .clr(reset));
  Register #(.width(16)) register_7 (.D(data), .en(demultiplexer_1_out6), .Q(out_12), .clk(clock), .clr(reset));
  Register #(.width(16)) register_8 (.D(data), .en(demultiplexer_1_out7), .Q(out_13), .clk(clock), .clr(reset));
  Register #(.width(16)) register_9 (.D(data), .en(demultiplexer_1_out8), .Q(out_14), .clk(clock), .clr(reset));
  Register #(.width(16)) register_10 (.D(data), .en(demultiplexer_1_out9), .Q(out_15), .clk(clock), .clr(reset));
  Register #(.width(16)) register_11 (.D(data), .en(demultiplexer_1_out10), .Q(out_16), .clk(clock), .clr(reset));
  Register #(.width(16)) register_12 (.D(data), .en(demultiplexer_1_out11), .Q(out_17), .clk(clock), .clr(reset));
  Register #(.width(16)) register_13 (.D(data), .en(demultiplexer_1_out12), .Q(out_18), .clk(clock), .clr(reset));
  Register #(.width(16)) register_14 (.D(data), .en(demultiplexer_1_out13), .Q(out_19), .clk(clock), .clr(reset));
  Register #(.width(16)) register_15 (.D(data), .en(demultiplexer_1_out14), .Q(out_20), .clk(clock), .clr(reset));
  Register #(.width(16)) register_16 (.D(data), .en(demultiplexer_1_out15), .Q(out_21), .clk(clock), .clr(reset));
endmodule

module Address_Decoder (
  input  [15:0] Address,
  output RAM,
  output FB_LED,
  output TTY,
  output output_3
);

  Decoder #(.select(2)) decoder_1 (
    .out0(RAM), .out1(FB_LED), .out2(TTY), .out3(output_3), .sel(Address[15:14]), .en(1'b1));
endmodule

module Counters (
  input  new_ucounter,
  input  reset,
  input  clock,
  output [15:0] cycles,
  output [3:0] icycles,
  output [15:0] cmds
);

  wire not_1_out;

  not not_1 (not_1_out, new_ucounter);
  Counter #(.max('hffff), .width(16)) counter_1 (
    .Q(cycles), .clk(clock), .clr(reset));  // open: load, D, count, carry, up
  Counter #(.max('hf), .width(4)) counter_2 (
    .load(not_1_out), .D(4'b0000), .Q(icycles), .clk(clock), .clr(reset));  // open: count, carry, up
  Counter #(.max('hffff), .width(16)) counter_3 (
    .count(not_1_out), .Q(cmds), .clk(clock), .clr(reset));  // open: load, D, carry, up
  // Probe on cycles
  // Probe on icycles
  // Probe on cmds

  // Notes on the sheet:
  //   Counts the number of clock cycles
  //   since the start.
  //   Counts the number of clock cycles
  //   since the start of current instruction.
  //   Counts the number of instructions
  //   since the start.
  //   Cycle/Cmds Counters
endmodule

module DebugUnit (
  input  reset,
  input  \continue ,
  input  clock,
  input  [15:0] pcreg,
  input  [15:0] break_addr,
  input  break_on_addr,
  input  ucounter,
  input  break_on_instr,
  input  break_on_cycle,
  output clock_out
);

  wire and_1_out, and_2_out, and_3_out, nor_1_out, nor_2_out, not_1_out, or_1_out, shift_register_1_out,
       shift_register_1_q0;
  wire [15:0] xor_1_out;

  Shift_Register #(.length(2), .trigger("falling")) shift_register_1 (
    .in(\continue ), .clk(clock), .out(shift_register_1_out), .clr(reset), .q0(shift_register_1_q0));  // open: shift, load, d0, d1, q1
  assign xor_1_out = pcreg ^ break_addr;  // XOR_Gate xor_1, 16 bits wide
  LED Addr (.in(break_on_addr));
  not not_1 (not_1_out, ucounter);
  and and_1 (and_1_out, ~shift_register_1_out, shift_register_1_q0);  // AND_Gate
  nor nor_1 (nor_1_out, xor_1_out[15], xor_1_out[14], xor_1_out[13], xor_1_out[12], xor_1_out[11], xor_1_out[10], xor_1_out[9], xor_1_out[8], xor_1_out[6], xor_1_out[5], xor_1_out[4], xor_1_out[3], xor_1_out[2], xor_1_out[1], xor_1_out[0], xor_1_out[7]);
  and and_2 (and_2_out, nor_1_out, break_on_addr, not_1_out);
  and and_3 (and_3_out, not_1_out, break_on_instr);
  LED Instr (.in(break_on_instr));
  LED Cycle (.in(break_on_cycle));
  nor nor_2 (nor_2_out, and_2_out, and_3_out, break_on_cycle);
  or or_1 (or_1_out, and_1_out, nor_2_out);
  LED Pass (.in(or_1_out));
  and and_4 (clock_out, clock, or_1_out);

  // Notes on the sheet:
  //   Breaks on PC = break_addr
  //   Breaks on each new instruction
  //   Breaks on each clock pulse
  //   Makes sure the 'continue' button only
  //   lets through 1 clock pulse, until you let go
  //   and press it again.
  //   Outputs 1 only on first cycle (shift bits are unequal).
  //   Debug Unit
  //   PC = break_addr?
endmodule

module ControlUnit_HW (
  input  [3:0] opcode,
  input  clock,
  input  reset,
  input  [3:0] Condition,
  input  carry,
  input  negative,
  input  oVerflow,
  input  zero,
  output [1:0] aluop,
  output readwrite,
  output phase,
  output [1:0] addrsel,
  output dwrite,
  output [1:0] regsel,
  output pcsel,
  output irload,
  output pcr,
  output pcload,
  output shiften
);

  wire and_4_out, conditionlogic_1_result, is_b, is_brc;

  T_Flip_Flop t_ff_1 (.T(1'b1), .clk(clock), .Q(phase), .reset(reset));  // open: Qn, preset
  and and_1 (is_b, ~opcode[0], ~opcode[1], ~opcode[2], opcode[3]);  // AND_Gate
  and and_2 (is_brc, opcode[0], ~opcode[1], ~opcode[2], opcode[3]);  // AND_Gate
  Multiplexer #(.enable("true"), .select(4), .width(2)) multiplexer_1 (
    .in0(2'b00), .in1(2'b00), .in2(2'b00), .in3(2'b00), .in4(2'b10), .in5(2'b10), .in6(2'b00), .in7(2'b00),
    .in8(2'b00), .in9(2'b00), .in10(2'b00), .in11(2'b00), .in12(2'b00), .in13(2'b00), .in14(2'b00),
    .in15(2'b00), .out(addrsel), .sel(opcode), .en(phase));
  and and_3 (readwrite, opcode[0], ~opcode[1], opcode[2], phase);  // AND_Gate
  Multiplexer #(.enable("true"), .select(4)) multiplexer_2 (
    .in0(1'b1), .in1(1'b1), .in2(1'b1), .in3(1'b1), .in4(1'b1), .in5(1'b0), .in6(1'b1), .in7(1'b1),
    .in8(1'b0), .in9(1'b0), .in10(1'b0), .in11(1'b0), .in12(1'b0), .in13(1'b0), .in14(1'b0), .in15(1'b0),
    .out(dwrite), .sel(opcode), .en(phase));
  ConditionLogic conditionlogic_1 (
    .Condition(Condition), .C(carry), .N(negative), .V(oVerflow), .Z(zero), .Result(conditionlogic_1_result));
  and and_4 (and_4_out, is_brc, conditionlogic_1_result);
  Multiplexer #(.enable("true"), .select(4), .width(2)) multiplexer_3 (
    .in0(2'b11), .in1(2'b11), .in2(2'b11), .in3(2'b11), .in4(2'b10), .in5(2'b00), .in6(2'b00), .in7(2'b01),
    .in8(2'b01), .in9(2'b01), .in10(2'b00), .in11(2'b00), .in12(2'b00), .in13(2'b00), .in14(2'b00),
    .in15(2'b00), .out(regsel), .sel(opcode), .en(phase));
  or or_1 (pcload, ~phase, is_b, and_4_out);  // OR_Gate
  not not_1 (irload, phase);
  or or_2 (pcsel, is_brc, irload);
  and and_5 (pcr, phase, is_brc);
  Multiplexer #(.enable("true"), .select(4)) multiplexer_4 (
    .in0(1'b0), .in1(1'b0), .in2(1'b0), .in3(1'b0), .in4(1'b0), .in5(1'b0), .in6(1'b1), .in7(1'b1),
    .in8(1'b0), .in9(1'b0), .in10(1'b0), .in11(1'b0), .in12(1'b0), .in13(1'b0), .in14(1'b0), .in15(1'b0),
    .out(shiften), .sel(opcode), .en(phase));

  assign aluop = opcode[1:0];

  // Notes on the sheet:
  //   Phase
  //   Address Select
  //   Read/Write (write for str)
  //   Dest Reg Write
  //   PC load?
  //   Register Select
  //   Constants
  //   PC operation
  //   PC increment source
  //   Shifter enable
endmodule

module ConditionLogic (
  input  [3:0] Condition,
  input  C,
  input  N,
  input  V,
  input  Z,
  output Result
);

  wire and_1_out, and_2_out, not_1_out, not_2_out, not_3_out, not_4_out, or_1_out, or_2_out, xor_1_out,
       xor_2_out;

  xor xor_1 (xor_1_out, N, V);
  and and_1 (and_1_out, C, ~Z);  // AND_Gate
  or or_1 (or_1_out, ~C, Z);  // OR_Gate
  xor xor_2 (xor_2_out, ~N, V);  // XOR_Gate
  and and_2 (and_2_out, xor_2_out, ~Z);  // AND_Gate
  or or_2 (or_2_out, Z, xor_1_out);
  not not_1 (not_1_out, Z);
  not not_2 (not_2_out, C);
  not not_3 (not_3_out, N);
  not not_4 (not_4_out, V);
  Multiplexer #(.select(4)) multiplexer_1 (
    .in0(Z), .in1(not_1_out), .in2(C), .in3(not_2_out), .in4(N), .in5(not_3_out), .in6(V), .in7(not_4_out),
    .in8(and_1_out), .in9(or_1_out), .in10(xor_2_out), .in11(xor_1_out), .in12(and_2_out), .in13(or_2_out),
    .in14(1'b0), .in15(1'b1), .out(Result), .sel(Condition));
endmodule

module movMagic (
  input  [15:0] w_in,
  input  [3:0] shift,
  input  a,
  input  dir,
  input  negate,
  input  enable,
  output [15:0] w_out
);

  wire [15:0] multiplexer_1_out, multiplexer_2_out, multiplexer_3_out, not_1_out, shifter_1_out,
       shifter_2_out, shifter_3_out;

  Shifter #(.width(16)) shifter_1 (.in(w_in), .\dist (shift), .out(shifter_1_out));
  Shifter #(.shift("lr"), .width(16)) shifter_2 (.in(w_in), .\dist (shift), .out(shifter_2_out));
  Shifter #(.shift("ar"), .width(16)) shifter_3 (.in(w_in), .\dist (shift), .out(shifter_3_out));
  Multiplexer #(.width(16)) multiplexer_1 (
    .in0(shifter_1_out), .in1(multiplexer_2_out), .out(multiplexer_1_out), .sel(dir));
  Multiplexer #(.width(16)) multiplexer_2 (.in0(shifter_2_out), .in1(shifter_3_out), .out(multiplexer_2_out), .sel(a));
  assign not_1_out = ~multiplexer_1_out;  // NOT_Gate not_1, 16 bits wide
  Multiplexer #(.width(16)) multiplexer_3 (
    .in0(multiplexer_1_out), .in1(not_1_out), .out(multiplexer_3_out), .sel(negate));
  Multiplexer #(.width(16)) multiplexer_4 (.in0(w_in), .in1(multiplexer_3_out), .out(w_out), .sel(enable));
endmodule
